// Logisim project alu.circ as structural Verilog: 3 circuits, main circuit main
module main (
  input  [15:0] X,
  input  [15:0] Y,
  input  [3:0] Switch__S,
  output Signed_Overflow,
  output [15:0] RESULT,
  output Equal
);

  wire ADDOVER, ADDOVER2, L1, SUBOVER, SUBOVER2;
  wire [15:0] adder_1_out, and_1_out, L2, n2add_1_out, n2sub_1_out, or_1_out, shifter_1_out, shifter_2_out,
       shifter_3_out, subtractor_1_out;

  Adder #(.width(16)) adder_1 (.a(X), .b(Y), .out(adder_1_out), .cout(ADDOVER));  // open: cin
  Subtractor #(.width(16)) subtractor_1 (.a(X), .b(Y), .out(subtractor_1_out), .bout(SUBOVER));  // open: bin
  Shifter #(.width(16)) shifter_1 (.in(X), .\dist (Y[3:0]), .out(shifter_1_out));
  Shifter #(.width(16), .shift("lr")) shifter_2 (.in(X), .\dist (Y[3:0]), .out(shifter_2_out));
  Shifter #(.width(16), .shift("ar")) shifter_3 (.in(X), .\dist (Y[3:0]), .out(shifter_3_out));
  Comparator #(.width(16)) comparator_1 (.a(X), .b(Y), .lt(L1));  // open: gt, eq
  assign or_1_out = X | Y;  // OR_Gate or_1, 16 bits wide
  assign and_1_out = X & Y;  // AND_Gate and_1, 16 bits wide
  _2ADD u_2add_1 (.in_1(X), .in_2(Y), .out(n2add_1_out), .out_2(ADDOVER2));
  _2SUB u_2sub_1 (.in_1(X), .in_2(Y), .out(n2sub_1_out), .out_2(SUBOVER2));
  Multiplexer #(.select(4), .width(16), .enable("false")) multiplexer_1 (
    .in0(adder_1_out), .in1(subtractor_1_out), .in2(shifter_1_out), .in3(shifter_2_out), .in4(shifter_3_out),
    .in5(L2), .in6(or_1_out), .in7(and_1_out), .in8(n2add_1_out), .in9(n2sub_1_out), .in15(X), .out(RESULT),
    .sel(Switch__S));  // open: in10, in11, in12, in13, in14
  Comparator #(.width(16)) comparator_2 (.a(X), .b(Y), .eq(Equal));  // open: gt, lt
  or or_2 (Signed_Overflow, ADDOVER, SUBOVER, ADDOVER2, SUBOVER2);
  Multiplexer #(.width(16), .enable("false")) multiplexer_2 (.in0({16{1'b0}}), .in1(16'h1), .out(L2), .sel(L1));

  // Other names for the same wires on the sheet: EQ = Equal; SWITCH[3:0] = Switch__S; Y2[3:0] = Y[3:0]

  // Notes on the sheet:
  //   INPUT to your circuit
  //   DON'T CHANGE THE INPUTS AND OUTPUTS! IF YOU DO SO, YOU NEED TO MAKE SURE THE PINS ARE IN THE RIGHT PLACES!
  //   OUTPUTS of your circuit
endmodule

module _2ADD (
  input  [15:0] in_1,
  input  [15:0] in_2,
  output [15:0] out,
  output out_2
);

  wire adder_1_cout, adder_2_cout;

  Adder adder_1 (.a(in_1[7:0]), .b(in_2[7:0]), .out(out[7:0]), .cout(adder_1_cout));  // open: cin
  Adder adder_2 (.a(in_1[15:8]), .b(in_2[15:8]), .out(out[15:8]), .cout(adder_2_cout));  // open: cin
  or or_1 (out_2, adder_2_cout, adder_1_cout);
endmodule

module _2SUB (
  input  [15:0] in_1,
  input  [15:0] in_2,
  output [15:0] out,
  output out_2
);

  wire subtractor_1_bout, subtractor_2_bout;

  Subtractor subtractor_1 (.a(in_1[7:0]), .b(in_2[7:0]), .out(out[7:0]), .bout(subtractor_1_bout));  // open: bin
  Subtractor subtractor_2 (.a(in_1[15:8]), .b(in_2[15:8]), .out(out[15:8]), .bout(subtractor_2_bout));  // open: bin
  or or_1 (out_2, subtractor_2_bout, subtractor_1_bout);
endmodule
