// Logisim project cpu.circ as structural Verilog: 11 circuits, main circuit main
module main (
  input  [15:0] From_Instr_Mem,
  input  clk,
  output [15:0] r0,
  output [15:0] r1,
  output [15:0] r2,
  output [15:0] r3,
  output [15:0] Display_0,
  output [15:0] Display_1,
  output [15:0] To_Instr_Mem,
  output [15:0] Data_Mem_Data,
  output [15:0] Data_Mem_Addr,
  output Data_Mem_Write
);

  wire ADDI, ANDI, BEQ, BNE, BRANCH, BRANCHIT, demultiplexer_1_out0, demultiplexer_1_out1, DISP, EQ, EQUAL,
       FUNCT, J, JAL, JR, JUMP, LUI, LW, MEMLOAD, NOPE, ORI, OVFLW, RGWRITE, RS_RT_IMM, RS_RT_RD_FUNCT,
       RS_UNUSED, RTYPE, SIGNED, SOURCE, SW;
  wire [1:0] multiplexer_12_out, multiplexer_13_out, RD, RS, RT;
  wire [3:0] OPCODE;
  wire [5:0] FUNCT_t, multiplexer_7_out, multiplexer_8_out, multiplexer_10_out;
  wire [7:0] IMM;
  wire [11:0] TARGETADDR;
  wire [15:0] adder_1_out, bit_extender_1_out, bit_extender_2_out, IMMTYPE, MEMOUT, multiplexer_1_out,
       multiplexer_2_out, multiplexer_3_out, multiplexer_4_out, multiplexer_9_out, multiplexer_11_out,
       multiplexer_14_out, multiplexer_15_out, NEXTPC, OLDPC, register_2_q, shifter_1_out, TOALU;

  SOURCE source_1 (.OPCODE(OPCODE), .out_2(SOURCE));
  JUMP jump_1 (.OPCODE(OPCODE), .out_2(JUMP));
  TYPE type_1 (.OPCODE(OPCODE), .out_2(RS_RT_RD_FUNCT), .out_3(FUNCT), .out_4(RS_UNUSED), .out_5(RS_RT_IMM));
  OPCODES opcodes_1 (
    .opcode(OPCODE), .RTYPE(RTYPE), .JAL(JAL), .J(J), .JR(JR), .BEQ(BEQ), .ADDI(ADDI), .ANDI(ANDI),
    .ORI(ORI), .BNE(BNE), .SW(SW), .LUI(LUI), .LW(LW), .DISP(DISP));
  BRANCH branch_1 (.OPCODE(OPCODE), .out_2(BRANCH));
  REGISTERWRITE registerwrite_1 (.OPCODE(OPCODE), .out_2(RGWRITE));
  MEMWRITE memwrite_1 (.OPCODE(OPCODE), .out_2(Data_Mem_Write));
  MEMLOAD memload_1 (.OPCODE(OPCODE), .out_2(MEMLOAD));
  SIGNED signed_1 (.OPCODE(OPCODE), .out_2(SIGNED));
  Multiplexer #(.width(16), .enable("false")) multiplexer_1 (
    .in0({16{1'b0}}), .in1(TOALU), .out(multiplexer_1_out), .sel(DISP));
  Demultiplexer #(.enable("false")) demultiplexer_1 (
    .out0(demultiplexer_1_out0), .out1(demultiplexer_1_out1), .in(DISP), .sel(IMMTYPE[0]));
  Register #(.width(16)) register_1 (
    .D(multiplexer_1_out), .en(demultiplexer_1_out0), .Q(Display_0), .clk(clk));  // open: clr
  Hex_Digit_Display hex_digit_display_1 (.value(Display_0[7:4]));  // open: dp
  Hex_Digit_Display hex_digit_display_2 (.value(Display_0[3:0]));  // open: dp
  assign bit_extender_1_out = {{8{1'b0}}, IMM};  // Bit_Extender bit_extender_1
  assign bit_extender_2_out = {{8{IMM[7]}}, IMM};  // Bit_Extender bit_extender_2
  Multiplexer #(.width(16), .enable("false")) multiplexer_2 (
    .in0(From_Instr_Mem), .in1(16'h6), .out(multiplexer_2_out), .sel(NOPE));
  Hex_Digit_Display hex_digit_display_3 (.value(Display_0[11:8]));  // open: dp
  Hex_Digit_Display hex_digit_display_4 (.value(Display_0[15:12]));  // open: dp
  Multiplexer #(.width(16), .enable("false")) multiplexer_3 (
    .in0(16'h1), .in1(IMMTYPE), .out(multiplexer_3_out), .sel(BRANCHIT));
  INSTRUCTIONS instructions_1 (
    .in_1(register_2_q), .FUNCT(FUNCT_t), .RD(RD), .RT(RT), .RS(RS), .IMM(IMM), .OPCODE(OPCODE),
    .TARGET_ADDR(TARGETADDR));
  Register #(.width(16)) register_2 (.D(multiplexer_2_out), .Q(register_2_q), .clk(clk));  // open: en, clr
  LED led_1 (.in(OVFLW));
  Hex_Digit_Display hex_digit_display_5 (.value(Display_1[3:0]));  // open: dp
  Register #(.width(16)) register_3 (
    .D(multiplexer_1_out), .en(demultiplexer_1_out1), .Q(Display_1), .clk(clk));  // open: clr
  Adder #(.width(16)) adder_1 (.a(To_Instr_Mem), .b(multiplexer_3_out), .out(adder_1_out));  // open: cin, cout
  Multiplexer #(.width(16), .enable("false")) multiplexer_4 (
    .in0({OLDPC[15:12], TARGETADDR}), .in1(TOALU), .out(multiplexer_4_out), .sel(JR));
  Multiplexer #(.width(16), .enable("false")) multiplexer_5 (
    .in0(bit_extender_1_out), .in1(bit_extender_2_out), .out(IMMTYPE), .sel(SIGNED));
  xor xor_1 (EQUAL, EQ, register_2_q[15]);
  Hex_Digit_Display hex_digit_display_6 (.value(Display_1[7:4]));  // open: dp
  Hex_Digit_Display hex_digit_display_7 (.value(Display_1[11:8]));  // open: dp
  Multiplexer #(.width(16), .enable("false")) multiplexer_6 (
    .in0(adder_1_out), .in1(multiplexer_4_out), .out(NEXTPC), .sel(JUMP));
  Hex_Digit_Display hex_digit_display_8 (.value(Display_1[15:12]));  // open: dp
  Register #(.width(16)) PC (.D(NEXTPC), .Q(To_Instr_Mem), .clk(clk));  // open: en, clr
  and and_1 (BRANCHIT, BRANCH, EQUAL);
  Multiplexer #(.width(6), .enable("false")) multiplexer_7 (
    .in0(FUNCT_t), .in1({6{1'b0}}), .out(multiplexer_7_out), .sel(SOURCE));
  Register #(.width(16)) OLD_PC (.D(To_Instr_Mem), .Q(OLDPC), .clk(clk));  // open: en, clr
  or or_1 (NOPE, BRANCHIT, JUMP);
  Multiplexer #(.width(6), .enable("false")) multiplexer_8 (
    .in0(multiplexer_7_out), .in1(6'b000111), .out(multiplexer_8_out), .sel(ANDI));
  RAM #(.addrWidth(16), .dataWidth(16), .bus("separate")) ram_1 (
    .addr(Data_Mem_Addr), .din(Data_Mem_Data), .data(MEMOUT), .str(Data_Mem_Write), .sel(1'b1), .clk(clk),
    .ld(MEMLOAD));  // open: clr
  // Probe on multiplexer_9_out
  // Probe on TOALU
  Multiplexer #(.width(16), .enable("false")) multiplexer_9 (
    .in0(Data_Mem_Data), .in1(IMMTYPE), .out(multiplexer_9_out), .sel(SOURCE));
  Multiplexer #(.width(6), .enable("false")) multiplexer_10 (
    .in0(multiplexer_8_out), .in1(6'b000110), .out(multiplexer_10_out), .sel(ORI));
  Multiplexer #(.width(16), .enable("false")) multiplexer_11 (
    .in0(Data_Mem_Addr), .in1(MEMOUT), .out(multiplexer_11_out), .sel(MEMLOAD));
  alu_main main_1 (
    .Switch__S(multiplexer_10_out[3:0]), .X(TOALU), .Equal(EQ), .RESULT(Data_Mem_Addr),
    .Signed_Overflow(OVFLW), .Y(multiplexer_9_out));
  // Probe on multiplexer_10_out
  Multiplexer #(.width(2), .enable("false")) multiplexer_12 (.in0(RT), .in1(RD), .out(multiplexer_12_out), .sel(RTYPE));
  Shifter #(.width(16)) shifter_1 (.in(IMMTYPE), .\dist (4'b1000), .out(shifter_1_out));
  // Probe on Data_Mem_Addr
  Multiplexer #(.width(2), .enable("false")) multiplexer_13 (
    .in0(multiplexer_12_out), .in1(2'b11), .out(multiplexer_13_out), .sel(JAL));
  Multiplexer #(.width(16), .enable("false")) multiplexer_14 (
    .in0(multiplexer_15_out), .in1(To_Instr_Mem), .out(multiplexer_14_out), .sel(JAL));
  Multiplexer #(.width(16), .enable("false")) multiplexer_15 (
    .in0(multiplexer_11_out), .in1(shifter_1_out), .out(multiplexer_15_out), .sel(LUI));
  Regfile_main main_2 (
    .Read_register_1(RS), .Read_register_2(RT), .write_register(multiplexer_13_out),
    .write_data(multiplexer_14_out), .Reg_0_Value(r0), .Reg_1_Value(r1), .Reg_2_Value(r2), .Reg_3_Value(r3),
    .RegWrite(RGWRITE), .clock(clk), .Read_Data_1(TOALU), .Read_Data_2(Data_Mem_Data));

  // Other names for the same wires on the sheet: ALURESULT[15:0] = Data_Mem_Addr; d0[15:0] = Display_0;
  //   d1[15:0] = Display_1; MEMWRITE = Data_Mem_Write; PC[15:0] = To_Instr_Mem; TOALU2[15:0] = Data_Mem_Data

  // Notes on the sheet:
  //   This is the current PC that you need to send as OUTPUT
  //   This is the instruction that you would receive as INPUT
  //   This is a CLK that is an INPUT driven from the harness.
  //   Remember, this circuit is loaded from the harness to be tested!
  //   DO NOT CHANGE THE LOCATIONS OF THE INPUTS OR OUTPUTS! IF YOU DO SO, YOU NEED TO MAKE SURE THE PINS ARE IN THE RIGHT PLACES!
  //   These are OUTPUTS of the circuit
  //   Data RAM
  //   These are OUTPUTS of the circuit
endmodule

module INSTRUCTIONS (
  input  [15:0] in_1,
  output [5:0] FUNCT,
  output [1:0] RD,
  output [1:0] RT,
  output [1:0] RS,
  output [7:0] IMM,
  output [3:0] OPCODE,
  output [11:0] TARGET_ADDR
);


  assign FUNCT = in_1[5:0];
  assign IMM = in_1[7:0];
  assign OPCODE = in_1[15:12];
  assign RD = in_1[7:6];
  assign RS = in_1[11:10];
  assign RT = in_1[9:8];
  assign TARGET_ADDR = in_1[11:0];
endmodule

module OPCODES (
  input  [3:0] opcode,
  output RTYPE,
  output JAL,
  output J,
  output JR,
  output BEQ,
  output ADDI,
  output ANDI,
  output ORI,
  output BNE,
  output SW,
  output LUI,
  output LW,
  output DISP
);

  Demultiplexer #(.select(4), .enable("false")) demultiplexer_1 (
    .out0(RTYPE), .out1(JAL), .out2(J), .out3(JR), .out4(BEQ), .out5(ADDI), .out6(ANDI), .out7(ORI),
    .out8(BNE), .out9(SW), .out10(LUI), .out11(LW), .out12(DISP), .in(1'b1), .sel(opcode));  // open: out13, out14, out15
endmodule

module REGISTERWRITE (
  input  [3:0] OPCODE,
  output out_2
);

  Multiplexer #(.select(4), .enable("false")) multiplexer_1 (
    .in0(1'b1), .in1(1'b1), .in2(1'b0), .in3(1'b0), .in4(1'b0), .in5(1'b1), .in6(1'b1), .in7(1'b1),
    .in8(1'b0), .in9(1'b0), .in10(1'b1), .in11(1'b1), .in12(1'b0), .out(out_2), .sel(OPCODE));  // open: in13, in14, in15
endmodule

module MEMWRITE (
  input  [3:0] OPCODE,
  output out_2
);

  Multiplexer #(.select(4), .enable("false")) multiplexer_1 (
    .in0(1'b0), .in1(1'b0), .in2(1'b0), .in3(1'b0), .in4(1'b0), .in5(1'b0), .in6(1'b0), .in7(1'b0),
    .in8(1'b0), .in9(1'b1), .in10(1'b0), .in11(1'b0), .in12(1'b0), .out(out_2), .sel(OPCODE));  // open: in13, in14, in15
endmodule

module MEMLOAD (
  input  [3:0] OPCODE,
  output out_2
);

  Multiplexer #(.select(4), .enable("false")) multiplexer_1 (
    .in0(1'b0), .in1(1'b0), .in2(1'b0), .in3(1'b0), .in4(1'b0), .in5(1'b0), .in6(1'b0), .in7(1'b0),
    .in8(1'b0), .in9(1'b0), .in10(1'b0), .in11(1'b1), .in12(1'b0), .out(out_2), .sel(OPCODE));  // open: in13, in14, in15
endmodule

module TYPE (
  input  [3:0] OPCODE,
  output out_2,
  output out_3,
  output out_4,
  output out_5
);

  wire [1:0] multiplexer_1_out;

  Multiplexer #(.select(4), .width(2), .enable("false")) multiplexer_1 (
    .in0(2'b00), .in1(2'b01), .in2(2'b01), .in3(2'b10), .in4(2'b11), .in5(2'b11), .in6(2'b11), .in7(2'b11),
    .in8(2'b11), .in9(2'b11), .in10(2'b11), .in11(2'b11), .in12(2'b11), .out(multiplexer_1_out), .sel(OPCODE));  // open: in13, in14, in15
  Demultiplexer #(.select(2), .enable("false")) demultiplexer_1 (
    .out0(out_2), .out1(out_3), .out2(out_4), .out3(out_5), .in(1'b1), .sel(multiplexer_1_out));
endmodule

module SIGNED (
  input  [3:0] OPCODE,
  output out_2
);

  Multiplexer #(.select(4), .enable("false")) multiplexer_1 (
    .in0(1'b0), .in1(1'b0), .in2(1'b0), .in3(1'b0), .in4(1'b1), .in5(1'b1), .in6(1'b0), .in7(1'b0),
    .in8(1'b1), .in9(1'b1), .in10(1'b0), .in11(1'b1), .in12(1'b0), .in13(1'b0), .in14(1'b0), .in15(1'b0),
    .out(out_2), .sel(OPCODE));
endmodule

module BRANCH (
  input  [3:0] OPCODE,
  output out_2
);

  Multiplexer #(.select(4), .enable("false")) multiplexer_1 (
    .in0(1'b0), .in1(1'b0), .in2(1'b0), .in3(1'b0), .in4(1'b1), .in5(1'b0), .in6(1'b0), .in7(1'b0),
    .in8(1'b1), .in9(1'b0), .in10(1'b0), .in11(1'b0), .in12(1'b0), .in13(1'b0), .in14(1'b0), .in15(1'b0),
    .out(out_2), .sel(OPCODE));
endmodule

module JUMP (
  input  [3:0] OPCODE,
  output out_2
);

  Multiplexer #(.select(4), .enable("false")) multiplexer_1 (
    .in0(1'b0), .in1(1'b1), .in2(1'b1), .in3(1'b1), .in4(1'b0), .in5(1'b0), .in6(1'b0), .in7(1'b0),
    .in8(1'b0), .in9(1'b0), .in10(1'b0), .in11(1'b0), .in12(1'b0), .in13(1'b0), .in14(1'b0), .in15(1'b0),
    .out(out_2), .sel(OPCODE));
endmodule

module SOURCE (
  input  [3:0] OPCODE,
  output out_2
);

  Multiplexer #(.select(4), .enable("false")) multiplexer_1 (
    .in0(1'b0), .in1(1'b0), .in2(1'b0), .in3(1'b0), .in4(1'b0), .in5(1'b1), .in6(1'b1), .in7(1'b1),
    .in8(1'b0), .in9(1'b1), .in10(1'b0), .in11(1'b1), .in12(1'b0), .in13(1'b0), .in14(1'b0), .in15(1'b0),
    .out(out_2), .sel(OPCODE));
endmodule
